# Fritzing sketch Sketch (saved by Fritzing 0.9.3b)
breadboards: 1

parts:
  R1 = Resistor [tolerance=±5% resistance=470 package=THT]
  U3 = ATTINY13 [package=dip]
  LED1 = LED - 5mm [color="Red (633nm)" package="5 mm [THT]"]
  S1 = Pushbutton [package="[THT]"]

nets:
  N1: R1.Pin_0, U3.PB3(ADC3), S1.Pin_1, S1.Pin_2
  N2: R1.Pin_1, LED1.cathode
  N3: U3.GND, LED1.anode, S1.Pin_3, S1.Pin_4

notes:
  Power
  GND
  ATtiny85 interrupt & sleep
